# Fritzing sketch esquema_parqueo_ESPACIOS (saved by Fritzing 0.9.4)
breadboards: 1

parts:
  Part2 = KY-016 RGB Full Color LED Module [package="Breakout board"]
  Power_plug1 = USB-C plug  # not connected
  A1 = Raspberry Pi Pico W
  Componente1 = SRF05 Ultrasonic Rangefinder
  SERVO1 = Tower Pro SG90 servo [part_number=101246]  # not connected

nets:
  N1: Part2.-, A1.pin_3, A1.pin_8, A1.pin_13, A1.pin_18, A1.pin_23, A1.pin_28, A1.pin_33, A1.pin_38, Componente1.GND
  N2: Part2.R, A1.pin_9
  N3: Part2.G, A1.pin_10
  N4: Part2.B, A1.pin_11
  N5: A1.pin_4, Componente1.Trig
  N6: A1.pin_5, Componente1.Echo
  N7: A1.pin_36, Componente1.VCC

custom parts:
  KY-016 RGB Full Color LED Module: KY-016 Arduino full color 5mm RGB LED, different colors can be obtained by mixing the three primary colors.
  USB-C plug: power plug
  Raspberry Pi Pico W: Raspberry Pi Pico W. Based around the RP2040 microcontroller the Pico W is a low cost microcontroller device bringing Raspberry Pi quality, cost, and easy of use to the microcontroller space. The areas marked KEEPOUT in pcb silkscreen should not have traces running through them to avoid shorts on a soldered in module!
  Tower Pro SG90 servo: Original file by John De Cristofaro http://www.adafruit.com/products/1449 Adafruit Feedback Servo (Small) Edited by: e-radionica.com 28/9/2015
